# Fritzing sketch Wiring_Diagram (saved by Fritzing 1.0.6)
breadboards: 1

parts:
  Mod1 = Raspberry Pi 4B
  Part2 = Breadboard Power Supply Board SMD
  HC-SR04_Sensor_1 = HC-SR04 Ultrasonic Distance Sensor
  Capacitive_Soil_Moisture_Sensor1 = DFRobot Capacitive Soil Moisture Sensor V1.0 [part_number=SEN0193]
  MPX4250AP1 = MPX4250AP pressure sensor [part_number=MPX]
  Part5 = Adafruit ADS1115 16Bit I2C ADC [part_number="Adafruit #1085"]
  MPX4250AP2 = MPX4250AP pressure sensor [part_number=MPX]
  Part6 = I2C level shifter bidirectional

nets:
  N1: Mod1.GPIO2, Part5.SDA
  N2: Mod1.GPIO3, Part5.SCL
  GND: Mod1.GND, Part2.GND, HC-SR04_Sensor_1.GND, Capacitive_Soil_Moisture_Sensor1.GND, MPX4250AP1.GND, Part5.GND, MPX4250AP2.GND, Part6.GND
  N3: Mod1.GPIO17, Part6.LV2
  VCC: Part2.VCC, HC-SR04_Sensor_1.VCC, Capacitive_Soil_Moisture_Sensor1.VCC, MPX4250AP1.Vs, Part5.VDD, MPX4250AP2.Vs, Part6.LV, Part6.HV
  N4: HC-SR04_Sensor_1.TRIG, Part6.HV2
  N5: HC-SR04_Sensor_1.ECHO, Part6.HV1
  N6: Capacitive_Soil_Moisture_Sensor1.A, Part5.AIN0
  N7: MPX4250AP1.V_out, Part6.HV3
  N8: Part5.AIN2, Part6.LV4
  N9: Part5.AIN1, Part6.LV3
  N10: MPX4250AP2.V_out, Part6.HV4

custom parts:
  DFRobot Capacitive Soil Moisture Sensor V1.0: DFRobot Capacitive Soil Moisture Sensor V1.0 This product measures soil moisture levels by capacitive sensing, rather than resistive sensing like other types of moisture sensor. It is made of a corrosion resistant material giving it a long service life. Insert it into soil and impress your friends with the real-time soil moisture data! The product includes an on-board voltage regulator which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
  Adafruit ADS1115 16Bit I2C ADC: For microcontrollers without an analog-to-digital converter or when you want a higher-precision ADC, the ADS1115 provides 16-bit precision at 860 samples/second over I2C. The chip can be configured as 4 single-ended input channels, or two differential channels. As a nice bonus, it even includes a programmable gain amplifier, up to x16, to help boost up smaller single/differential signals to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
